// Logisim project s-mips.circ as structural Verilog: 6 circuits, main circuit S-MIPS Board
module S_MIPS_Board (
  input  DESHABILITAR_DISPATCHER,
  output halt
);

  wire button_1_out, CLK, CS, d_ff_1_q, LCLR, LoadRAM, LoadRAMOn, LW, R_R_W, R_W, ram_dispatcher_1_finished,
       RCS, Reset_out, RST, TTY_EN;
  wire [2:0] KDB;
  wire [3:0] LMask, Mask, ram_1_read_time, ram_1_write_time, RMask;
  wire [6:0] KDB_DATA, TTY_DATA;
  wire [15:0] Addr, LAddr, RAddr;
  wire [31:0] I0, I1, I2, I3, LData, ram_1_data_out_0, ram_1_data_out_1, ram_1_data_out_2, ram_1_data_out_3,
       RI0, RI1, RI2, RI3;

  TTY #(.rows(25), .cols(80)) tty_1 (.data(TTY_DATA), .clk(CLK), .we(TTY_EN), .clr(RST));
  not not_1 (LoadRAMOn, ram_dispatcher_1_finished);
  RAM_Dispatcher ram_dispatcher_1 (
    .WriteTime(ram_1_write_time), .Clock(CLK), .Data(LData), .Address(LAddr), .Mask(LMask),
    .Finished(ram_dispatcher_1_finished), .Write(LW), .CLR(LCLR));
  Keyboard #(.buflen(64)) keyboard_1 (.clk(CLK), .re(KDB[0]), .avail(KDB[2]), .data(KDB_DATA));  // open: clr
  RAM ram_1 (
    .Address(RAddr), .Data_Out_0(ram_1_data_out_0), .Data_Out_1(ram_1_data_out_1),
    .Data_Out_2(ram_1_data_out_2), .Data_Out_3(ram_1_data_out_3), .Data_In_0(RI0), .Data_In_1(RI1),
    .Data_In_2(RI2), .Data_In_3(RI3), .Mask(RMask), .nRead_Write(R_R_W), .Chip_Select(RCS),
    .Read_Time(ram_1_read_time), .Reset(button_1_out), .Write_Time(ram_1_write_time));
  Button button_1 (.out(button_1_out));
  D_Flip_Flop d_ff_1 (.clk(CLK), .D(1'b1), .Q(d_ff_1_q), .reset(Reset_out));  // open: Qn, preset, en
  Button Reset (.out(Reset_out));
  S_MIPS s_mips_1 (
    .Kbd_Enable(KDB[0]), .Address(Addr), .Kbd_Clear(KDB[1]), .Kbd_Available(KDB[2]), .RAM_In_0(I0),
    .Kbd_ASCII_Data(KDB_DATA), .RAM_In_1(I1), .TTY_Enable(TTY_EN), .RAM_In_2(I2), .RAM_In_3(I3),
    .TTY_ASCII_Data(TTY_DATA), .Reset(RST), .RAM_Out_0(ram_1_data_out_0), .Clock(CLK),
    .RAM_Out_1(ram_1_data_out_1), .Stop(halt), .RAM_Out_2(ram_1_data_out_2), .RAM_Out_3(ram_1_data_out_3),
    .Mask(Mask), .Read_Time(ram_1_read_time), .Write_Time(ram_1_write_time), .nRead_Write(R_W),
    .Chip_Select(CS));
  D_Flip_Flop d_ff_2 (.clk(CLK), .D(d_ff_1_q), .Qn(LCLR), .reset(Reset_out));  // open: Q, preset, en
  or or_1 (RST, LCLR, LoadRAM);
  Clock clock_1 (.out(CLK));
  Multiplexer #(.width(32), .enable("false")) multiplexer_1 (.in0(I0), .in1(LData), .out(RI0), .sel(LoadRAM));
  Multiplexer #(.width(32), .enable("false")) multiplexer_2 (.in0(I1), .in1(LData), .out(RI1), .sel(LoadRAM));
  Multiplexer #(.width(32), .enable("false")) multiplexer_3 (.in0(I2), .in1(LData), .out(RI2), .sel(LoadRAM));
  Multiplexer #(.width(32), .enable("false")) multiplexer_4 (.in0(I3), .in1(LData), .out(RI3), .sel(LoadRAM));
  and and_1 (LoadRAM, ~DESHABILITAR_DISPATCHER, LoadRAMOn);  // AND_Gate
  Multiplexer #(.width(16), .enable("false")) multiplexer_5 (.in0(Addr), .in1(LAddr), .out(RAddr), .sel(LoadRAM));
  Multiplexer #(.width(4), .enable("false")) multiplexer_6 (.in0(Mask), .in1(LMask), .out(RMask), .sel(LoadRAM));
  Multiplexer #(.enable("false")) multiplexer_7 (.in0(CS), .in1(LW), .out(RCS), .sel(LoadRAM));
  Multiplexer #(.enable("false")) multiplexer_8 (.in0(R_W), .in1(LW), .out(R_R_W), .sel(LoadRAM));

  // Notes on the sheet:
  //   NO MODIFICAR
  //   Keyboard
endmodule

module RAM (
  input  [15:0] Address,
  input  [31:0] Data_In_0,
  input  [31:0] Data_In_1,
  input  [31:0] Data_In_2,
  input  [31:0] Data_In_3,
  input  [3:0] Mask,
  input  nRead_Write,
  input  Chip_Select,
  input  Reset,
  output [31:0] Data_Out_0,
  output [31:0] Data_Out_1,
  output [31:0] Data_Out_2,
  output [31:0] Data_Out_3,
  output [3:0] Read_Time,
  output [3:0] Write_Time
);

  wire and_2_out, and_3_out, and_4_out, and_5_out, and_6_out, and_7_out, and_8_out, and_9_out, Changed, CLK,
       comparator_2_eq, comparator_3_eq, comparator_4_eq, comparator_5_eq, comparator_6_eq, Count,
       demultiplexer_3_out0, Idle, Idle_q, Load, Load0, Load1, nand_1_out, or_1_out, or_2_out, or_3_out,
       or_4_out, or_5_out, or_6_out, or_7_out, or_8_out, or_9_out, or_10_out, Proc_q, Update_Mem, Zero_Time;
  wire [3:0] counter_1_q, multiplexer_1_out, subtractor_1_out;
  wire [31:0] register_1_q, register_2_q, register_3_q, register_4_q, register_5_q;

  // Probe on 4'b0011
  // Probe on 4'b0010
  Multiplexer #(.width(4), .enable("false")) multiplexer_1 (
    .in0(4'b0011), .in1(4'b0010), .out(multiplexer_1_out), .sel(nRead_Write));
  or or_1 (or_1_out, Idle, Update_Mem);
  or or_2 (or_2_out, ~Chip_Select, Reset);  // OR_Gate
  Subtractor #(.width(4)) subtractor_1 (.a(multiplexer_1_out), .b(4'b0010), .out(subtractor_1_out));  // open: bin, bout
  Demultiplexer #(.enable("false")) demultiplexer_1 (.out0(Idle), .out1(Load0), .in(Idle_q), .sel(Changed));
  D_Flip_Flop u_Idle (.clk(CLK), .D(or_1_out), .Q(Idle_q), .preset(or_2_out));  // open: Qn, en, reset
  // Probe on counter_1_q
  Counter #(.width(4), .max('hf)) counter_1 (
    .load(Load), .D(subtractor_1_out), .count(Count), .Q(counter_1_q), .clk(CLK), .clr(or_3_out));  // open: carry
  or or_3 (or_3_out, ~Chip_Select, Reset);  // OR_Gate
  Comparator #(.width(4), .mode("unsigned")) comparator_1 (
    .a(4'b0000), .b(counter_1_q), .eq(Zero_Time));  // open: gt, lt
  or or_4 (or_4_out, Count, Load0, Load1);
  Register_part #(.width(32)) register_1 (.D(Data_In_0), .en(Chip_Select), .Q(register_1_q), .clk(CLK), .clr(or_5_out));
  or or_5 (or_5_out, ~Chip_Select, Reset);  // OR_Gate
  Register_part #(.width(32)) register_2 (.D(Data_In_1), .en(Chip_Select), .Q(register_2_q), .clk(CLK), .clr(or_6_out));
  or or_6 (or_6_out, ~Chip_Select, Reset);  // OR_Gate
  Register_part #(.width(32)) register_3 (.D(Data_In_2), .en(Chip_Select), .Q(register_3_q), .clk(CLK), .clr(or_7_out));
  or or_7 (or_7_out, ~Chip_Select, Reset);  // OR_Gate
  Register_part #(.width(32)) register_4 (.D(Data_In_3), .en(Chip_Select), .Q(register_4_q), .clk(CLK), .clr(or_8_out));
  or or_8 (or_8_out, ~Chip_Select, Reset);  // OR_Gate
  Register_part #(.width(32)) register_5 (
    .D({{11{1'b1}}, nRead_Write, Mask, Address}), .en(Chip_Select), .Q(register_5_q), .clk(CLK),
    .clr(or_9_out));
  or or_9 (or_9_out, ~Chip_Select, Reset);  // OR_Gate
  D_Flip_Flop Proc (.clk(CLK), .D(or_4_out), .Q(Proc_q), .reset(or_10_out));  // open: Qn, preset, en
  or or_10 (or_10_out, ~Chip_Select, Reset);  // OR_Gate
  Demultiplexer #(.enable("false")) demultiplexer_2 (
    .out0(Count), .out1(Update_Mem), .in(demultiplexer_3_out0), .sel(Zero_Time));
  Demultiplexer #(.enable("false")) demultiplexer_3 (
    .out0(demultiplexer_3_out0), .out1(Load1), .in(Proc_q), .sel(Changed));
  Clock clock_1 (.out(CLK));
  Comparator #(.width(32)) comparator_2 (.a(register_1_q), .b(Data_In_0), .eq(comparator_2_eq));  // open: gt, lt
  Comparator #(.width(32)) comparator_3 (.a(register_2_q), .b(Data_In_1), .eq(comparator_3_eq));  // open: gt, lt
  Comparator #(.width(32)) comparator_4 (.a(register_3_q), .b(Data_In_2), .eq(comparator_4_eq));  // open: gt, lt
  Comparator #(.width(32)) comparator_5 (.a(register_4_q), .b(Data_In_3), .eq(comparator_5_eq));  // open: gt, lt
  Comparator #(.width(32)) comparator_6 (
    .a(register_5_q), .b({{11{1'b1}}, nRead_Write, Mask, Address}), .eq(comparator_6_eq));  // open: gt, lt
  nand nand_1 (nand_1_out, comparator_6_eq, comparator_2_eq, comparator_3_eq, comparator_4_eq, comparator_5_eq);
  and and_1 (Changed, nand_1_out, Chip_Select);
  or or_11 (Load, Count, Load1, Load0);
  and and_2 (and_2_out, Mask[0], Update_Mem, nRead_Write);
  and and_3 (and_3_out, Mask[1], Update_Mem, nRead_Write);
  and and_4 (and_4_out, Mask[2], Update_Mem, nRead_Write);
  and and_5 (and_5_out, Mask[3], Update_Mem, nRead_Write);
  RAM_part #(.addrWidth(16), .dataWidth(32), .bus("separate")) ram_1 (
    .addr(Address), .din(Data_In_0), .data(Data_Out_0), .str(and_2_out), .sel(Chip_Select), .clk(CLK),
    .ld(and_6_out), .clr(Reset));
  and and_6 (and_6_out, ~nRead_Write, Idle);  // AND_Gate
  RAM_part #(.addrWidth(16), .dataWidth(32), .bus("separate")) ram_2 (
    .addr(Address), .din(Data_In_1), .data(Data_Out_1), .str(and_3_out), .sel(Chip_Select), .clk(CLK),
    .ld(and_7_out), .clr(Reset));
  and and_7 (and_7_out, ~nRead_Write, Idle);  // AND_Gate
  RAM_part #(.addrWidth(16), .dataWidth(32), .bus("separate")) ram_3 (
    .addr(Address), .din(Data_In_2), .data(Data_Out_2), .str(and_4_out), .sel(Chip_Select), .clk(CLK),
    .ld(and_8_out), .clr(Reset));
  and and_8 (and_8_out, ~nRead_Write, Idle);  // AND_Gate
  RAM_part #(.addrWidth(16), .dataWidth(32), .bus("separate")) ram_4 (
    .addr(Address), .din(Data_In_3), .data(Data_Out_3), .str(and_5_out), .sel(Chip_Select), .clk(CLK),
    .ld(and_9_out), .clr(Reset));
  and and_9 (and_9_out, ~nRead_Write, Idle);  // AND_Gate

  assign Read_Time = 4'b0011;
  assign Write_Time = 4'b0010;

  // Other names for the same wires on the sheet: M0 = Mask[0]; M1 = Mask[1]; M2 = Mask[2]; M3 = Mask[3];
  //   RW = nRead_Write; CLR = Reset; CS = Chip_Select; Load2 = Count

  // Notes on the sheet:
  //   NO MODIFICAR
  //   excepto quizás los valores RT y WT
  //   BANK0
  //   BANK1
  //   BANK2
  //   BANK3
endmodule

module S_MIPS (
  input  Kbd_Available,
  input  [6:0] Kbd_ASCII_Data,
  input  [31:0] RAM_Out_0,
  input  [31:0] RAM_Out_1,
  input  Reset,
  input  [31:0] RAM_Out_2,
  input  Clock,
  input  [31:0] RAM_Out_3,
  input  [3:0] Read_Time,
  input  [3:0] Write_Time,
  output Kbd_Enable,
  output [15:0] Address,
  output Kbd_Clear,
  output TTY_Enable,
  output [6:0] TTY_ASCII_Data,
  output Stop,
  output [31:0] RAM_In_0,
  output [31:0] RAM_In_1,
  output [31:0] RAM_In_2,
  output [31:0] RAM_In_3,
  output [3:0] Mask,
  output nRead_Write,
  output Chip_Select
);


  // Other names for the same wires on the sheet: CLK = Clock; CLR = Reset; CS = Chip_Select;
  //   KBD_AVAIL = Kbd_Available; KBD_CLR = Kbd_Clear; KBD_DATA[6:0] = Kbd_ASCII_Data; RAM_A[15:0] = Address;
  //   RAM_INPUT_0[31:0] = RAM_In_0; RAM_INPUT_1[31:0] = RAM_In_1; RAM_INPUT_2[31:0] = RAM_In_2;
  //   RAM_INPUT_3[31:0] = RAM_In_3; RAM_MASK[3:0] = Mask; RAM_OUTPUT_0[31:0] = RAM_Out_0;
  //   RAM_OUTPUT_1[31:0] = RAM_Out_1; RAM_OUTPUT_2[31:0] = RAM_Out_2; RAM_OUTPUT_3[31:0] = RAM_Out_3;
  //   RW = nRead_Write; TTY_DATA[6:0] = TTY_ASCII_Data

  // Notes on the sheet:
  //   RAM ADDRESS
  //   DATA FROM RAM
  //   DATA TO RAM
  //   DATA WRITE MASK
  //   RAM TIMING
  //   RAM CONTROL
  //   KEYBOARD
  //   TTY
  //   SEQUENCING
endmodule

module RAM_Dispatcher (
  input  [3:0] WriteTime,
  input  Clock,
  input  CLR,
  output [31:0] Data,
  output [15:0] Address,
  output [3:0] Mask,
  output Finished,
  output Write
);

  wire demultiplexer_2_out1, demultiplexer_3_out1, End, IDLE_q, IncAddr, Load, or_1_out, or_2_out, While_q,
       WriteEnd;
  wire [3:0] counter_1_q;
  wire [31:0] CurrentAddress_q;

  Counter #(.width(32), .max('hffffffff)) CurrentAddress (
    .count(IncAddr), .Q({CurrentAddress_q[31:18], Address, CurrentAddress_q[1:0]}), .clk(Clock), .clr(CLR));  // open: load, D, carry
  or or_1 (or_1_out, IncAddr, demultiplexer_3_out1, Finished);
  D_Flip_Flop IDLE (.clk(Clock), .D(or_1_out), .Q(IDLE_q), .preset(CLR));  // open: Qn, en, reset
  Demultiplexer #(.enable("false")) demultiplexer_1 (.out0(Load), .out1(Finished), .in(IDLE_q), .sel(End));
  D_Flip_Flop While (.clk(Clock), .D(or_2_out), .Q(While_q), .reset(CLR));  // open: Qn, preset, en
  or or_2 (or_2_out, Write, Load);
  RAM_part #(.addrWidth(18), .dataWidth(32)) ram_1 (
    .addr({Address, CurrentAddress_q[1:0]}), .data(Data), .clk(Clock));  // open: sel, ld, clr
  Demultiplexer #(.enable("false")) demultiplexer_2 (
    .out0(Write), .out1(demultiplexer_2_out1), .in(While_q), .sel(WriteEnd));
  Decoder #(.select(2)) decoder_1 (
    .out0(Mask[0]), .out1(Mask[1]), .out2(Mask[2]), .out3(Mask[3]), .sel(CurrentAddress_q[1:0]));  // open: en
  Demultiplexer #(.enable("false")) demultiplexer_3 (
    .out0(IncAddr), .out1(demultiplexer_3_out1), .in(demultiplexer_2_out1), .sel(End));
  Counter #(.width(4), .max('hf)) counter_1 (
    .load(Load), .D(WriteTime), .count(Write), .Q(counter_1_q), .clk(Clock));  // open: carry, clr
  Comparator #(.width(32)) comparator_1 (.a(Data), .b({32{1'b1}}), .eq(End));  // open: gt, lt
  Comparator #(.width(4)) comparator_2 (.a(4'b0000), .b(counter_1_q), .eq(WriteEnd));  // open: gt, lt

  // Other names for the same wires on the sheet: CLK = Clock; Count = Write; WT[3:0] = WriteTime
endmodule

module Register (
  input  in_1,
  input  in_2,
  input  in_3,
  input  [31:0] in_4,
  input  [31:0] in_5,
  input  [4:0] DataAdress,
  input  [4:0] SelectorA,
  input  [4:0] SelectorB,
  input  Enable_High_Low,
  input  Enable_PC,
  input  Pop,
  input  Push,
  input  [31:0] HighInput,
  input  [31:0] in_14,
  input  [31:0] SP,
  output [31:0] Low,
  output [31:0] High
);

  wire E_SP, to0, to1, to2, to3, to4, to5, to6, to7, to8, to9, to10, to11, to12, to13, to14, to15, to16,
       to17, to18, to19, to20, to21, to22, to23, to24, to25, to26, to27, to28, to29, to30, to31;
  wire [31:0] output0, output1, output2, output3, output4, output5, output6, output7, output8, output9,
       output10, output11, output12, output13, output14, output15, output16, output17, output18, output19,
       output20, output21, output22, output23, output24, output25, output26, output27, output28, output29,
       output30, SP_Input, SPOutput, SPoutput_t, undriven, undriven_2;

  Demultiplexer #(.select(5)) demultiplexer_1 (
    .out0(to0), .out1(to1), .out2(to2), .out3(to3), .out4(to4), .out5(to5), .out6(to6), .out7(to7),
    .out8(to8), .out9(to9), .out10(to10), .out11(to11), .out12(to12), .out13(to13), .out14(to14),
    .out15(to15), .out16(to16), .out17(to17), .out18(to18), .out19(to19), .out20(to20), .out21(to21),
    .out22(to22), .out23(to23), .out24(to24), .out25(to25), .out26(to26), .out27(to27), .out28(to28),
    .out29(to29), .out30(to30), .out31(to31), .in(in_1), .sel(DataAdress));  // open: en
  Register_part #(.width(32)) R0 (.D(undriven), .en(to0), .Q(output0), .clk(in_2), .clr(in_3));
  Register_part #(.width(32)) R4 (.D(in_4), .en(to4), .Q(output4), .clk(in_2), .clr(in_3));
  Register_part #(.width(32)) R8 (.D(in_4), .en(to8), .Q(output8), .clk(in_2), .clr(in_3));
  Register_part #(.width(32)) R12 (.D(in_4), .en(to12), .Q(output12), .clk(in_2), .clr(in_3));
  Register_part #(.width(32)) R16 (.D(in_4), .en(to16), .Q(output16), .clk(in_2), .clr(in_3));
  Register_part #(.width(32)) R20 (.D(in_4), .en(to20), .Q(output20), .clk(in_2), .clr(in_3));
  Register_part #(.width(32)) R24 (.D(in_4), .en(to24), .Q(output24), .clk(in_2), .clr(in_3));
  Register_part #(.width(32)) R28 (.D(in_4), .en(to28), .Q(output28), .clk(in_2), .clr(in_3));
  Register_part #(.width(32)) R1 (.D(in_4), .en(to1), .Q(output1), .clk(in_2), .clr(in_3));
  Register_part #(.width(32)) R5 (.D(in_4), .en(to5), .Q(output5), .clk(in_2), .clr(in_3));
  Register_part #(.width(32)) R9 (.D(in_4), .en(to9), .Q(output9), .clk(in_2), .clr(in_3));
  Register_part #(.width(32)) R13 (.D(in_4), .en(to13), .Q(output13), .clk(in_2), .clr(in_3));
  Register_part #(.width(32)) R17 (.D(in_4), .en(to17), .Q(output17), .clk(in_2), .clr(in_3));
  Register_part #(.width(32)) R21 (.D(in_4), .en(to21), .Q(output21), .clk(in_2), .clr(in_3));
  Register_part #(.width(32)) R25 (.D(in_4), .en(to25), .Q(output25), .clk(in_2), .clr(in_3));
  Register_part #(.width(32)) R29 (.D(in_4), .en(to29), .Q(output29), .clk(in_2), .clr(in_3));
  Register_part #(.width(32)) R2 (.D(in_4), .en(to2), .Q(output2), .clk(in_2), .clr(in_3));
  Register_part #(.width(32)) R6 (.D(in_4), .en(to6), .Q(output6), .clk(in_2), .clr(in_3));
  Register_part #(.width(32)) R10 (.D(in_4), .en(to10), .Q(output10), .clk(in_2), .clr(in_3));
  Register_part #(.width(32)) R14 (.D(in_4), .en(to14), .Q(output14), .clk(in_2), .clr(in_3));
  Register_part #(.width(32)) R18 (.D(in_4), .en(to18), .Q(output18), .clk(in_2), .clr(in_3));
  Register_part #(.width(32)) R22 (.D(in_4), .en(to22), .Q(output22), .clk(in_2), .clr(in_3));
  Register_part #(.width(32)) R26 (.D(in_4), .en(to26), .Q(output26), .clk(in_2), .clr(in_3));
  Register_part #(.width(32)) R30 (.D(in_4), .en(to30), .Q(output30), .clk(in_2), .clr(in_3));
  Register_part #(.width(32)) u_High (.D(HighInput), .en(Enable_High_Low), .Q(High), .clk(in_2), .clr(in_3));
  Register_part #(.width(32)) u_Low (.D(undriven_2), .en(Enable_High_Low), .Q(Low), .clk(in_2), .clr(in_3));
  Register_part #(.width(32)) R3 (.D(in_4), .en(to3), .Q(output3), .clk(in_2), .clr(in_3));
  Register_part #(.width(32)) R7 (.D(in_4), .en(to7), .Q(output7), .clk(in_2), .clr(in_3));
  Register_part #(.width(32)) R11 (.D(in_4), .en(to11), .Q(output11), .clk(in_2), .clr(in_3));
  Register_part #(.width(32)) R15 (.D(in_4), .en(to15), .Q(output15), .clk(in_2), .clr(in_3));
  Register_part #(.width(32)) R19 (.D(in_4), .en(to19), .Q(output19), .clk(in_2), .clr(in_3));
  Register_part #(.width(32)) R23 (.D(in_4), .en(to23), .Q(output23), .clk(in_2), .clr(in_3));
  Register_part #(.width(32)) R27 (.D(in_4), .en(to27), .Q(output27), .clk(in_2), .clr(in_3));
  Register_part #(.width(32)) u_SP (.D(SP_Input), .en(E_SP), .Q(SPoutput_t), .clk(in_2), .clr(in_3));
  Multiplexer #(.select(5), .width(32)) multiplexer_1 (
    .in0(output0), .in1(output1), .in2(output2), .in3(output3), .in4(output4), .in5(output5), .in6(output6),
    .in7(output7), .in8(output8), .in9(output9), .in10(output10), .in11(output11), .in12(output12),
    .in13(output13), .in14(output14), .in15(output15), .in16(output16), .in17(output17), .in18(output18),
    .in19(output19), .in20(output20), .in21(output21), .in22(output22), .in23(output23), .in24(output24),
    .in25(output25), .in26(output26), .in27(output27), .in28(output28), .in29(output29), .in30(output30),
    .in31(SPoutput_t), .out(in_5), .sel(SelectorA));  // open: en
  Multiplexer #(.select(5), .width(32)) multiplexer_2 (
    .in0(output0), .in1(output1), .in2(output2), .in3(output3), .in4(output4), .in5(output5), .in6(output6),
    .in7(output7), .in8(output8), .in9(output9), .in10(output10), .in11(output11), .in12(output12),
    .in13(output13), .in14(output14), .in15(output15), .in16(output16), .in17(output17), .in18(output18),
    .in19(output19), .in20(output20), .in21(output21), .in22(output22), .in23(output23), .in24(output24),
    .in25(output25), .in26(output26), .in27(output27), .in28(output28), .in29(output29), .in30(output30),
    .in31(SPOutput), .out(in_14), .sel(SelectorB));  // open: en

  // Other names for the same wires on the sheet: Clock = in_2; Data_Input[31:0] = in_4; E_HL = Enable_High_Low;
  //   E_PC = Enable_PC; High_Input[31:0] = HighInput; R_W = in_1; Reset = in_3
endmodule

module Program_Counter (
  input  in_1,
  input  in_2,
  input  in_3,
  input  in_4,
  input  [15:0] in_5,
  input  [25:0] in_6,
  input  [31:0] in_7,
  input  in_8,
  input  in_9,
  output [31:0] out_10,
  output [31:0] out_11
);

  wire and_2_out, not_1_out;
  wire [25:0] shifter_1_out;
  wire [31:0] bit_extender_1_out, Branch_Adress, Jump_Adress, Output, PC_High, PCNext_Branch, shifter_2_out,
       TargetShifted;

  Adder #(.width(32)) adder_1 (.a(out_10), .b(32'h4), .out(out_11));  // open: cin, cout
  assign bit_extender_1_out = {{16{in_5[15]}}, in_5};  // Bit_Extender bit_extender_1
  Shifter #(.width(26)) shifter_1 (.in(in_6), .\dist (5'b00010), .out(shifter_1_out));
  Shifter #(.width(32)) shifter_2 (.in(bit_extender_1_out), .\dist (5'b00010), .out(shifter_2_out));
  assign TargetShifted = {{6{1'b0}}, shifter_1_out};  // Bit_Extender bit_extender_2
  Adder #(.width(32)) adder_2 (.a(out_11), .b(shifter_2_out), .out(Branch_Adress));  // open: cin, cout
  assign PC_High = out_11 & 32'hf0000000;  // AND_Gate and_1, 32 bits wide
  assign Jump_Adress = PC_High | TargetShifted;  // OR_Gate or_1, 32 bits wide
  Multiplexer #(.width(32)) multiplexer_1 (
    .in0(out_11), .in1(Branch_Adress), .out(PCNext_Branch), .en(in_9));  // open: sel
  not not_1 (not_1_out, in_2);
  and and_2 (and_2_out, in_8, not_1_out);
  Multiplexer #(.select(2), .width(32)) multiplexer_2 (
    .in0(PCNext_Branch), .in1(Jump_Adress), .in2(in_7), .in3({32{1'b0}}), .out(Output));  // open: sel, en
  Register_part #(.width(32)) PC (.D(Output), .en(and_2_out), .Q(out_10), .clk(in_1), .clr(in_2));

  // Other names for the same wires on the sheet: BranchTaken = in_9; Clock = in_1; Jr = in_4; Jump = in_3;
  //   Offset[15:0] = in_5; PCOut[31:0] = out_10; PCplus4[31:0] = out_11; PCWrite = in_8; Reset = in_2;
  //   RsData[31:0] = in_7; Target[25:0] = in_6
endmodule
